# Fritzing sketch Untitled Sketch 2 (saved by Fritzing 1.0.6)
circuit board: 8.46667cm x 5.64444cm
breadboards: 1

parts:
  元件1 = Arduino Uno (Rev3)
  LED1 = LED - 5mm [color="Red (633nm)" current=0.030A package="5 mm [THT]"]
  LED2 = LED - 5mm [color="Red (633nm)" current=0.030A package="5 mm [THT]"]
  LED3 = LED - 5mm [color="Red (633nm)" current=0.030A package="5 mm [THT]"]
  LED5 = LED - 5mm [color="Red (633nm)" current=0.030A package="5 mm [THT]"]
  R1 = Resistor [tolerance=±5% power=0.25W resistance=220 package=THT]
  R2 = Resistor [tolerance=±5% power=0.25W resistance=220 package=THT]
  R3 = Resistor [tolerance=±5% power=0.25W resistance=220 package=THT]
  R4 = Resistor [tolerance=±5% power=0.25W resistance=220 package=THT]

nets:
  N1: 元件1.GND, LED1.cathode, LED2.cathode, LED3.cathode, LED5.cathode
  N2: 元件1.D4, R4.Pin_1
  N3: 元件1.D5_PWM, R3.Pin_1
  N4: 元件1.D6_PWM, R2.Pin_1
  N5: 元件1.D7, R1.Pin_1
  N6: LED1.anode, R1.Pin_0
  N7: LED2.anode, R2.Pin_0
  N8: LED3.anode, R3.Pin_0
  N9: LED5.anode, R4.Pin_0

// code stored in the sketch: Untitled2.ino
int ledPins[]={4,5,6,7};
int ledCount=4;
int delayTime=7;
void setup()
{
    for(int i=0;i<ledCount;i++)
    {
        pinMode(ledPins[i],OUTPUT);
    }
}
void loop()
{
    for(int i=0;i<ledCount;i++)
    {
        digitalWrite(ledPins[i],HIGH);
        delay(delayTime);
        digitalWrite(ledPins[i],LOW);
    }
}
